// Digital circuit ALU(32bits).dig as structural Verilog
module ALU_32bits (
  input  [31:0] InA,
  input  [31:0] InB,
  input  [3:0] Sel,
  output Ca,
  output Cs,
  output [31:0] Out,
  output [31:0] rdiv,
  output [31:0] rdivu
);

  wire slt, sltu;
  wire [31:0] add, \and , div, divu, mul, mulh, MULH_mul, mulhsu, MULHSU_mul, mulhu, MULHU_mul, \or , sll,
       sltex, sltuex, sra, srl, sub, \xor ;
  wire [63:32] MUL_mul;

  Add #(.Bits(32)) u_ADD (.a(InA), .b(InB), .c_i(1'b0), .s(add), .c_o(Ca));
  assign \xor  = InA ^ InB;  // XOr xor_1, 32 bits wide
  Sub #(.Bits(32)) u_SUB (.a(InA), .b(InB), .c_i(1'b0), .s(sub), .c_o(Cs));
  Mul #(.Bits(32)) u_MULHU (.a(InA), .b(InB), .mul({mulhu, MULHU_mul}));
  BarrelShifter #(.Bits(32), .barrelSigned("true")) u_SLL (.in(InA), .shift(InB[6:0]), .out(sll));
  BarrelShifter #(.Bits(32), .direction("right")) u_SRL (.in(InA), .shift(InB[5:0]), .out(srl));
  Mul #(.Signed("true"), .Bits(32)) u_MUL (.a(InA), .b(InB), .mul({MUL_mul, mul}));
  BarrelShifter #(.Bits(32), .barrelShifterMode("arithmetic"), .barrelSigned("true"), .direction("right")) u_SRA (
    .in(InA), .shift(InB[6:0]), .out(sra));
  Comparator #(.Signed("true"), .Bits(32)) u_SLT (.a(InA), .b(InB), .lt(slt));  // open: gt, eq
  assign \or  = InA | InB;  // Or or_1, 32 bits wide
  Mul #(.Signed("true"), .Bits(32)) u_MULH (.a(InA), .b(InB), .mul({mulh, MULH_mul}));
  Div #(.Bits(32)) u_DIV (.a(InA), .b(InB), .q(div), .r(rdiv));
  BitExtender #(.inputBits(1), .outputBits(32)) bitextender_1 (.in(slt), .out(sltex));
  Comparator #(.Bits(32)) u_SLTU (.a(InA), .b(InB), .lt(sltu));  // open: gt, eq
  assign \and  = InA & InB;  // And and_1, 32 bits wide
  Mul #(.Signed("true"), .Bits(32)) u_MULHSU (.a(InA), .b(InB), .mul({mulhsu, MULHSU_mul}));
  Div #(.Bits(32)) u_DIVU (.a(InA), .b(InB), .q(divu), .r(rdivu));
  BitExtender #(.inputBits(1), .outputBits(32)) bitextender_2 (.in(sltu), .out(sltuex));
  Multiplexer #(.Selector_Bits(4), .Bits(32)) multiplexer_1 (
    .sel(Sel), .in_0(add), .in_1(sll), .in_2(sltex), .in_3(sltuex), .in_4(\xor ), .in_5(srl), .in_6(\or ),
    .in_7(\and ), .in_8(sub), .in_9(mul), .in_10(mulh), .in_11(mulhsu), .in_12(mulhu), .in_13(sra),
    .in_14(div), .in_15(divu), .out(Out));

  // Other names for the same wires on the sheet: SHL[6:0] = InB[6:0]; SHR[5:0] = InB[5:0]

  // Notes on the sheet:
  //   InA: Entrada 1 para cualquier operación que se vaya a realizar
  //   InB: Entrada 2 para la operación que se vaya a realizar
  //   Ca: Almacena el acarreo de una suma
  //   Cs: Acarreo para la resta
  //   Sel: Permite seleccionar la operación que se quiere realizar
  //   Out: Salida dependiendo de la operación escogida
  //   rdiv: Acarreo para la resta
  //   rdivu: Acarreo para la resta
endmodule
