// Digital circuit RegisterUnit.dig as structural Verilog
module RegisterUnit (
  input  [4:0] RD,
  input  C,
  input  [4:0] RS1,
  input  [31:0] DataWr,
  input  [4:0] RS2,
  input  RuWr,
  output [31:0] RU_rs1,
  output [31:0] RU_rs2,
  output [31:0] a4,
  output [31:0] a5,
  output [31:0] a0,
  output [31:0] x0,
  output [31:0] s0
);

  wire x0_t, x1, x2, x3, x4, x5, x6, x7, x8, x9, x10, x11, x12, x13, x14, x15, x16, x17, x18, x19, x20, x21,
       x22, x23, x24, x25, x26, x27, x28, x29, x30, x31;
  wire [31:0] d1, d2, d3, d4, d5, d6, d7, d9, d11, d12, d13, d16, d17, d18, d19, d20, d21, d22, d23, d24,
       d25, d26, d27, d28, d29, d30, d31;

  Demultiplexer #(.Selector_Bits(5)) demultiplexer_1 (
    .sel(RD), .in(RuWr), .out_0(x0_t), .out_1(x1), .out_2(x2), .out_3(x3), .out_4(x4), .out_5(x5),
    .out_6(x6), .out_7(x7), .out_8(x8), .out_9(x9), .out_10(x10), .out_11(x11), .out_12(x12), .out_13(x13),
    .out_14(x14), .out_15(x15), .out_16(x16), .out_17(x17), .out_18(x18), .out_19(x19), .out_20(x20),
    .out_21(x21), .out_22(x22), .out_23(x23), .out_24(x24), .out_25(x25), .out_26(x26), .out_27(x27),
    .out_28(x28), .out_29(x29), .out_30(x30), .out_31(x31));
  Register #(.Bits(32)) u_x0 (.D(DataWr), .C(C), .en(x0_t), .Q(x0));
  Register #(.Bits(32)) u_x4 (.D(DataWr), .C(C), .en(x4), .Q(d4));
  Register #(.Bits(32)) u_x8 (.D(DataWr), .C(C), .en(x8), .Q(s0));
  Register #(.Bits(32)) u_x12 (.D(DataWr), .C(C), .en(x12), .Q(d12));
  Register #(.Bits(32)) u_x16 (.D(DataWr), .C(C), .en(x16), .Q(d16));
  Register #(.Bits(32)) u_x20 (.D(DataWr), .C(C), .en(x20), .Q(d20));
  Register #(.Bits(32)) u_x24 (.D(DataWr), .C(C), .en(x24), .Q(d24));
  Register #(.Bits(32)) u_x28 (.D(DataWr), .C(C), .en(x28), .Q(d28));
  Register #(.Bits(32)) u_x1 (.D(DataWr), .C(C), .en(x1), .Q(d1));
  Register #(.Bits(32)) u_x5 (.D(DataWr), .C(C), .en(x5), .Q(d5));
  Register #(.Bits(32)) u_x9 (.D(DataWr), .C(C), .en(x9), .Q(d9));
  Register #(.Bits(32)) u_x13 (.D(DataWr), .C(C), .en(x13), .Q(d13));
  Register #(.Bits(32)) u_x17 (.D(DataWr), .C(C), .en(x17), .Q(d17));
  Register #(.Bits(32)) u_x21 (.D(DataWr), .C(C), .en(x21), .Q(d21));
  Register #(.Bits(32)) u_x25 (.D(DataWr), .C(C), .en(x25), .Q(d25));
  Register #(.Bits(32)) u_x29 (.D(DataWr), .C(C), .en(x29), .Q(d29));
  Register #(.Bits(32)) u_x2 (.D(DataWr), .C(C), .en(x2), .Q(d2));
  Register #(.Bits(32)) u_x6 (.D(DataWr), .C(C), .en(x6), .Q(d6));
  Register #(.Bits(32)) u_x10 (.D(DataWr), .C(C), .en(x10), .Q(a0));
  Register #(.Bits(32)) u_x14 (.D(DataWr), .C(C), .en(x14), .Q(a4));
  Register #(.Bits(32)) u_x18 (.D(DataWr), .C(C), .en(x18), .Q(d18));
  Register #(.Bits(32)) u_x22 (.D(DataWr), .C(C), .en(x22), .Q(d22));
  Register #(.Bits(32)) u_x26 (.D(DataWr), .C(C), .en(x26), .Q(d26));
  Register #(.Bits(32)) u_x30 (.D(DataWr), .C(C), .en(x30), .Q(d30));
  Register #(.Bits(32)) u_x3 (.D(DataWr), .C(C), .en(x3), .Q(d3));
  Register #(.Bits(32)) u_x7 (.D(DataWr), .C(C), .en(x7), .Q(d7));
  Register #(.Bits(32)) u_x11 (.D(DataWr), .C(C), .en(x11), .Q(d11));
  Register #(.Bits(32)) u_x15 (.D(DataWr), .C(C), .en(x15), .Q(a5));
  Register #(.Bits(32)) u_x19 (.D(DataWr), .C(C), .en(x19), .Q(d19));
  Register #(.Bits(32)) u_x23 (.D(DataWr), .C(C), .en(x23), .Q(d23));
  Register #(.Bits(32)) u_x27 (.D(DataWr), .C(C), .en(x27), .Q(d27));
  Register #(.Bits(32)) u_x31 (.D(DataWr), .C(C), .en(x31), .Q(d31));
  Multiplexer #(.Selector_Bits(5), .Bits(32)) multiplexer_1 (
    .sel(RS1), .in_0(x0), .in_1(d1), .in_2(d2), .in_3(d3), .in_4(d4), .in_5(d5), .in_6(d6), .in_7(d7),
    .in_8(s0), .in_9(d9), .in_10(a0), .in_11(d11), .in_12(d12), .in_13(d13), .in_14(a4), .in_15(a5),
    .in_16(d16), .in_17(d17), .in_18(d18), .in_19(d19), .in_20(d20), .in_21(d21), .in_22(d22), .in_23(d23),
    .in_24(d24), .in_25(d25), .in_26(d26), .in_27(d27), .in_28(d28), .in_29(d29), .in_30(d30), .in_31(d31),
    .out(RU_rs1));
  Multiplexer #(.Selector_Bits(5), .Bits(32)) multiplexer_2 (
    .sel(RS2), .in_0(x0), .in_1(d1), .in_2(d2), .in_3(d3), .in_4(d4), .in_5(d5), .in_6(d6), .in_7(d7),
    .in_8(s0), .in_9(d9), .in_10(a0), .in_11(d11), .in_12(d12), .in_13(d13), .in_14(a4), .in_15(a5),
    .in_16(d16), .in_17(d17), .in_18(d18), .in_19(d19), .in_20(d20), .in_21(d21), .in_22(d22), .in_23(d23),
    .in_24(d24), .in_25(d25), .in_26(d26), .in_27(d27), .in_28(d28), .in_29(d29), .in_30(d30), .in_31(d31),
    .out(RU_rs2));

  // Other names for the same wires on the sheet: d0[31:0] = x0; d8[31:0] = s0; d10[31:0] = a0; d14[31:0] = a4;
  //   d15[31:0] = a5

  // Notes on the sheet:
  //   RD: Del rd de la instrucción tomada, para especificar el registro donde se desea escribir
  //   RS1: Se usa para leer el dato que hay en un registro específico. Se toma de los 5 bits que da la Instruction Memory
  //   DataWr: Dato proveniente del Data Memory que se va a escribir en el registro RD
  //   RU_rs1: Almacena la salida del rs1
  //   RS2: Se usa para leer el dato que hay en un registro específico. Se toma de los 5 bits que da la Instruction Memory
  //   RU_rs2: Almacena la salida del rs2
  //   RuWr: Habilita la escritura
endmodule
