// Digital circuit ResultSplitterDisplay.dig as structural Verilog
module ResultSplitterDisplay (
  input  [31:0] Result,
  output [3:0] R1,
  output [3:0] R2,
  output [3:0] R3,
  output [3:0] R4,
  output [3:0] R5,
  output [3:0] R6,
  output [3:0] R7,
  output [3:0] R8
);


  assign R1 = Result[3:0];
  assign R2 = Result[7:4];
  assign R3 = Result[11:8];
  assign R4 = Result[15:12];
  assign R5 = Result[19:16];
  assign R6 = Result[23:20];
  assign R7 = Result[27:24];
  assign R8 = Result[31:28];

  // Notes on the sheet:
  //   Result: Esta entrada se obtiene del registro a0 donde regularmente RISC-V mueve el resultado final de la operación.
  //   R1: División de cuatro bits
  //   R2: División de cuatro bits
  //   R3: División de cuatro bits
  //   R4: División de cuatro bits
  //   R5: División de cuatro bits
  //   R6: División de cuatro bits
  //   R7: División de cuatro bits
  //   R8: División de cuatro bits
endmodule
