// Digital circuit ControlUnit.dig as structural Verilog
// Cerebro del sistema. Establece las señales que toman decisiones dependiendo del tipo de instrucción y de operación
module ControlUnit (
  input  [6:0] Opcode,
  input  [2:0] Funct3,
  input  [6:0] Funct7,
  input  [4:0] rd,
  output RUWr,
  output [2:0] ImmSrc,
  output ALUASrc,
  output ALUBSrc,
  output DMWr,
  output [1:0] RUDataWrSrc,
  output [4:0] BrOp,
  output [2:0] DMCtrl,
  output [3:0] ALUOp
);

  wire add, addi, addO, \and , and_7_out, and_8_out, and_9_out, and_10_out, and_11_out, and_12_out,
       and_13_out, and_14_out, andi, B, Br1, Br2, Br3, Br4, Br5, Br6, comparator_1_eq, comparator_2_eq,
       comparator_3_eq, comparator_4_eq, comparator_5_eq, comparator_6_eq, comparator_8_eq, comparator_9_eq,
       comparator_10_eq, comparator_11_eq, comparator_12_eq, comparator_13_eq, div, divO, divu, divuO,
       DMCtrl_2_eq, DMCtrl_3_eq, F7A, F7B, F7C, I, IL, IS, J, mul, mulh, mulhO, mulhsu, mulhsuO, mulhu,
       mulhuO, mulO, \or , or_1_out, ori, R, rd_t, S, sll, slli, sllO, slt, slti, sltiu, sltO, sltu, sltuO,
       sra, srai, sraiO, sraO, srl, srli, srliO, srlO, sub, subO, U, \xor , xori, xorO;
  wire [2:0] DM, F3A, F3B;
  wire [3:0] Iop, Rop, Uop;
  wire [4:0] Br, BrB;

  Comparator #(.Bits(3)) comparator_1 (.a(Funct3), .b(3'b000), .eq(comparator_1_eq));  // open: gt, lt
  Comparator #(.Bits(3)) comparator_2 (.a(Funct3), .b(3'b001), .eq(comparator_2_eq));  // open: gt, lt
  Comparator #(.Bits(3)) comparator_3 (.a(Funct3), .b(3'b100), .eq(comparator_3_eq));  // open: gt, lt
  Comparator #(.Bits(3)) comparator_4 (.a(Funct3), .b(3'b101), .eq(comparator_4_eq));  // open: gt, lt
  Comparator #(.Bits(3)) comparator_5 (.a(Funct3), .b(3'b110), .eq(comparator_5_eq));  // open: gt, lt
  Comparator #(.Bits(3)) comparator_6 (.a(Funct3), .b(3'b111), .eq(comparator_6_eq));  // open: gt, lt
  Comparator #(.Bits(5)) comparator_7 (.a(rd), .b({5{1'b0}}), .eq(rd_t));  // open: gt, lt
  Comparator #(.Bits(7)) Tipo_R (.a(Opcode), .b(7'b0110011), .eq(R));  // open: gt, lt
  Comparator #(.Bits(7)) Tipo_I (.a(Opcode), .b(7'b0010011), .eq(I));  // open: gt, lt
  Comparator #(.Bits(7)) Tipo_I_lectura (.a(Opcode), .b(7'b0000011), .eq(IL));  // open: gt, lt
  Comparator #(.Bits(7)) Tipo_S (.a(Opcode), .b(7'b0100011), .eq(S));  // open: gt, lt
  Comparator #(.Bits(7)) Tipo_B (.a(Opcode), .b(7'b1100011), .eq(B));  // open: gt, lt
  Comparator #(.Bits(7)) Tipo_I_salto (.a(Opcode), .b(7'b1100111), .eq(IS));  // open: gt, lt
  Comparator #(.Bits(7)) Tipo_J (.a(Opcode), .b(7'b1101111), .eq(J));  // open: gt, lt
  Comparator #(.Bits(7)) Tipo_U (.a(Opcode), .b(7'b0110111), .eq(U));  // open: gt, lt
  and and_1 (Br1, comparator_1_eq, B);
  and and_2 (Br2, comparator_2_eq, B);
  and and_3 (Br3, comparator_3_eq, B);
  and and_4 (Br4, comparator_4_eq, B);
  and and_5 (Br5, comparator_5_eq, B);
  and and_6 (Br6, comparator_6_eq, B);
  LookUpTable #(.Bits(9)) lookuptable_1 (
    .in0(R), .in1(I), .in2(IL), .in3(S), .in4(B), .in5(IS), .in6(J), .in7(U), .in8(rd_t),
    .out({RUWr, ImmSrc, ALUASrc, ALUBSrc, DMWr, RUDataWrSrc}));
  LookUpTable #(.Bits(5)) Branch (.in0(R), .in1(I), .in2(IL), .in3(S), .in4(IS), .in5(J), .in6(U), .out(Br));
  LookUpTable #(.Bits(3)) u_DMCtrl (.in0(R), .in1(I), .in2(B), .in3(IS), .in4(J), .in5(U), .out(DM));
  Multiplexer #(.Bits(5)) multiplexer_1 (.sel(B), .in_0(Br), .in_1(BrB), .out(BrOp));
  LookUpTable #(.Bits(5)) BrTypeB (.in0(Br1), .in1(Br2), .in2(Br3), .in3(Br4), .in4(Br5), .in5(Br6), .out(BrB));
  Multiplexer #(.Selector_Bits(2), .Bits(3)) multiplexer_2 (
    .sel({S, IL}), .in_0(DM), .in_1(F3A), .in_2(F3B), .in_3(3'b000), .out(DMCtrl));
  Comparator #(.Bits(3)) DMCtrl_2 (.a(Funct3), .b(3'b000), .eq(DMCtrl_2_eq));  // open: gt, lt
  Comparator #(.Bits(3)) comparator_8 (.a(Funct3), .b(3'b001), .eq(comparator_8_eq));  // open: gt, lt
  Comparator #(.Bits(3)) comparator_9 (.a(Funct3), .b(3'b010), .eq(comparator_9_eq));  // open: gt, lt
  Comparator #(.Bits(3)) comparator_10 (.a(Funct3), .b(3'b100), .eq(comparator_10_eq));  // open: gt, lt
  Comparator #(.Bits(3)) comparator_11 (.a(Funct3), .b(3'b101), .eq(comparator_11_eq));  // open: gt, lt
  or or_1 (or_1_out, IL, S, B, IS, J);
  and and_7 (and_7_out, DMCtrl_2_eq, IL);
  and and_8 (and_8_out, comparator_8_eq, IL);
  and and_9 (and_9_out, comparator_9_eq, IL);
  and and_10 (and_10_out, comparator_10_eq, IL);
  and and_11 (and_11_out, comparator_11_eq, IL);
  LookUpTable #(.Bits(4)) Tipo_R_2 (
    .in0(addO), .in1(subO), .in2(sllO), .in3(sltO), .in4(sltuO), .in5(xorO), .in6(srlO), .in7(sraO),
    .in8(\or ), .in9(\and ), .in10(mulO), .in11(mulhO), .in12(mulhsuO), .in13(mulhuO), .in14(divO),
    .in15(divuO), .out(Rop));
  LookUpTable #(.Bits(4)) Tipo_I_2 (
    .in0(addi), .in1(slli), .in2(slti), .in3(sltiu), .in4(xori), .in5(srliO), .in6(sraiO), .in7(ori),
    .in8(andi), .out(Iop));
  LookUpTable #(.Bits(4)) lookuptable_2 (.in0(U), .in1(or_1_out), .out(Uop));
  LookUpTable #(.Bits(3)) lookuptable_3 (
    .in0(and_7_out), .in1(and_8_out), .in2(and_9_out), .in3(and_10_out), .in4(and_11_out), .out(F3A));
  Multiplexer #(.Selector_Bits(2), .Bits(4)) multiplexer_3 (
    .sel({R, I}), .in_0(Uop), .in_1(Iop), .in_2(Rop), .in_3(4'b0000), .out(ALUOp));
  Comparator #(.Bits(3)) DMCtrl_3 (.a(Funct3), .b(3'b000), .eq(DMCtrl_3_eq));  // open: gt, lt
  Comparator #(.Bits(3)) comparator_12 (.a(Funct3), .b(3'b001), .eq(comparator_12_eq));  // open: gt, lt
  Comparator #(.Bits(3)) comparator_13 (.a(Funct3), .b(3'b010), .eq(comparator_13_eq));  // open: gt, lt
  and and_12 (and_12_out, DMCtrl_3_eq, S);
  and and_13 (and_13_out, comparator_12_eq, S);
  and and_14 (and_14_out, comparator_13_eq, S);
  LookUpTable #(.Bits(3)) lookuptable_4 (.in0(and_12_out), .in1(and_13_out), .in2(and_14_out), .out(F3B));
  Comparator #(.Bits(3)) u_ADD (.a(Funct3), .b(3'b000), .eq(add));  // open: gt, lt
  Comparator #(.Bits(3)) u_SUB (.a(Funct3), .b(3'b000), .eq(sub));  // open: gt, lt
  Comparator #(.Bits(3)) u_SLL (.a(Funct3), .b(3'b001), .eq(sll));  // open: gt, lt
  Comparator #(.Bits(3)) u_SLT (.a(Funct3), .b(3'b010), .eq(slt));  // open: gt, lt
  Comparator #(.Bits(3)) u_SLTU (.a(Funct3), .b(3'b011), .eq(sltu));  // open: gt, lt
  Comparator #(.Bits(3)) u_XOR (.a(Funct3), .b(3'b100), .eq(\xor ));  // open: gt, lt
  Comparator #(.Bits(3)) u_SRL (.a(Funct3), .b(3'b101), .eq(srl));  // open: gt, lt
  Comparator #(.Bits(3)) u_SRA (.a(Funct3), .b(3'b101), .eq(sra));  // open: gt, lt
  Comparator #(.Bits(3)) OR_2 (.a(Funct3), .b(3'b110), .eq(\or ));  // open: gt, lt
  Comparator #(.Bits(3)) AND_15 (.a(Funct3), .b(3'b111), .eq(\and ));  // open: gt, lt
  Comparator #(.Bits(7)) comparator_14 (.a(Funct7), .b({7{1'b0}}), .eq(F7A));  // open: gt, lt
  Comparator #(.Bits(7)) comparator_15 (.a(Funct7), .b(7'b0100000), .eq(F7B));  // open: gt, lt
  and and_16 (addO, add, F7A);
  and and_17 (subO, sub, F7B);
  and and_18 (srlO, srl, F7A);
  and and_19 (sraO, sra, F7B);
  and and_20 (srliO, srli, F7A);
  and and_21 (sraiO, srai, F7B);
  Comparator #(.Bits(3)) u_ADDI (.a(Funct3), .b(3'b000), .eq(addi));  // open: gt, lt
  Comparator #(.Bits(3)) u_SLLI (.a(Funct3), .b(3'b001), .eq(slli));  // open: gt, lt
  Comparator #(.Bits(3)) u_SLTI (.a(Funct3), .b(3'b010), .eq(slti));  // open: gt, lt
  Comparator #(.Bits(3)) u_SLTIU (.a(Funct3), .b(3'b011), .eq(sltiu));  // open: gt, lt
  Comparator #(.Bits(3)) u_XORI (.a(Funct3), .b(3'b100), .eq(xori));  // open: gt, lt
  Comparator #(.Bits(3)) u_SRLI (.a(Funct3), .b(3'b101), .eq(srli));  // open: gt, lt
  Comparator #(.Bits(3)) u_SRAI (.a(Funct3), .b(3'b101), .eq(srai));  // open: gt, lt
  Comparator #(.Bits(3)) u_ORI (.a(Funct3), .b(3'b110), .eq(ori));  // open: gt, lt
  Comparator #(.Bits(3)) u_ANDI (.a(Funct3), .b(3'b111), .eq(andi));  // open: gt, lt
  Comparator #(.Bits(3)) u_MUL (.a(Funct3), .b(3'b000), .eq(mul));  // open: gt, lt
  Comparator #(.Bits(3)) u_MULH (.a(Funct3), .b(3'b001), .eq(mulh));  // open: gt, lt
  Comparator #(.Bits(3)) u_MULHSU (.a(Funct3), .b(3'b010), .eq(mulhsu));  // open: gt, lt
  Comparator #(.Bits(3)) u_MULHU (.a(Funct3), .b(3'b011), .eq(mulhu));  // open: gt, lt
  Comparator #(.Bits(3)) u_DIV (.a(Funct3), .b(3'b100), .eq(div));  // open: gt, lt
  Comparator #(.Bits(3)) u_DIVU (.a(Funct3), .b(3'b101), .eq(divu));  // open: gt, lt
  and and_22 (sllO, sll, F7A);
  and and_23 (sltO, slt, F7A);
  and and_24 (sltuO, sltu, F7A);
  and and_25 (xorO, \xor , F7A);
  Comparator #(.Bits(7)) comparator_16 (.a(Funct7), .b(7'b0000001), .eq(F7C));  // open: gt, lt
  and and_26 (mulO, mul, F7C);
  and and_27 (mulhO, mulh, F7C);
  and and_28 (mulhsuO, mulhsu, F7C);
  and and_29 (mulhuO, mulhu, F7C);
  and and_30 (divO, div, F7C);
  and and_31 (divuO, divu, F7C);

  // Other names for the same wires on the sheet: F3[2:0] = Funct3; F7[6:0] = Funct7

  // Notes on the sheet:
  //   Opcode: Define el tipo de instrucción a procesar
  //   Funct3: Define el tipo de operación y también el tipo de branch y DMCtrl
  //   Funct7: Diferencia entre add y sub, y entre sra y srl
  //   rd: RD necesario para identificar x0 a la hora de tener saltos incodicionales con registro de referencia a x0
  //   contents of lookuptable_1 (hex, n*v repeats v):
  //   0,1e0,108,0,109,0,0,0,2f,7*0,bb,15*0,10a,31*0,1da,63*0,48,71*0
  //   ,1,87*0,a,31*0,da
  //   contents of Branch (hex, n*v repeats v):
  //   0,7,7,0,7,0,0,0,7,7*0,10,15*0,10,31*0,7
  //   contents of DMCtrl (hex, n*v repeats v):
  //   0,7,7,0,7,0,0,0,7,7*0,7,15*0,7
  //   contents of BrTypeB (hex, n*v repeats v):
  //   0,8,a,0,b,0,0,0,8,7*0,d,15*0,e
  //   contents of Tipo_R_2 (hex, n*v repeats v):
  //   0,0,8,0,1,0,0,0,2,7*0,3,15*0,4,31*0,5,63*0,d,127*0,6,255*0,7,511*0
  //   ,9,1023*0,a,2047*0,b,4095*0,c,8191*0,e,16383*0,f
  //   contents of Tipo_I_2 (hex, n*v repeats v):
  //   0,0,1,0,2,0,0,0,3,7*0,4,15*0,5,31*0,d,63*0,6,127*0,7
  //   contents of lookuptable_2 (hex, n*v repeats v):
  //   0,7
  //   contents of lookuptable_3 (hex, n*v repeats v):
  //   0,6,5,0,4,0,0,0,2,7*0,1
  //   contents of lookuptable_4 (hex, n*v repeats v):
  //   0,6,5,0,4
endmodule
