// Digital circuit Monocycle_Style.dig as structural Verilog
module Monocycle_Style (
  input  CLK,
  input  reset,
  output out_1,
  output out_2,
  output [31:0] ImmExt,
  output [31:0] IMOut,
  output [31:0] OutPC,
  output [31:0] RU_rs1,
  output [31:0] RU_rs2,
  output [31:0] DMOut,
  output [31:0] a5,
  output [31:0] a4,
  output [31:0] x0,
  output [31:0] a0
);

  wire ALUASrc, ALUBSrc, branchunit_1_p4, DMWr, RUWr;
  wire [1:0] RUDataWrSrc;
  wire [2:0] DMCtrl, ImmSrc;
  wire [3:0] ALUOp, D1, D2, D3, D4, D5, D6, D7, D8, R1, R2, R3, R4, R5, R6, R7, R8;
  wire [4:0] BrOp;
  wire [31:0] ALUOut, DataWr, InPC, multiplexer_1_out, multiplexer_2_out, s0, SumPC;

  // ALUSplitterDisplay alusplitterdisplay_1: pin names not known; wires that end beside it: ALUOut, D1, D2, D3, D4, D5, D6, D7, D8
  PC_1 pc_1_1 (.clk(CLK), .InPC(InPC), .Reset(reset), .OutPC(OutPC));
  Seven_Seg_Hex seven_seg_hex_1 (.d(D8), .dp(1'b0));
  Seven_Seg_Hex seven_seg_hex_2 (.d(D7), .dp(1'b0));
  Seven_Seg_Hex seven_seg_hex_3 (.d(D6), .dp(1'b0));
  Add #(.Bits(32)) add_1 (.a(32'h4), .b(OutPC), .c_i(1'b0), .s(SumPC));  // open: c_o
  // InstructionMemory instructionmemory_1: pin names not known; wires that end beside it: OutPC[23:0], IMOut
  Seven_Seg_Hex seven_seg_hex_4 (.d(D5), .dp(1'b0));
  Seven_Seg_Hex seven_seg_hex_5 (.d(D4), .dp(1'b0));
  Seven_Seg_Hex seven_seg_hex_6 (.d(D3), .dp(1'b0));
  Seven_Seg_Hex seven_seg_hex_7 (.d(D2), .dp(1'b0));
  Seven_Seg_Hex seven_seg_hex_8 (.d(D1), .dp(1'b0));
  ControlUnit controlunit_1 (
    .Opcode(IMOut[6:0]), .Funct3(IMOut[14:12]), .Funct7(IMOut[31:25]), .rd(IMOut[11:7]), .RUWr(RUWr),
    .ImmSrc(ImmSrc), .ALUASrc(ALUASrc), .ALUBSrc(ALUBSrc), .DMWr(DMWr), .RUDataWrSrc(RUDataWrSrc),
    .BrOp(BrOp), .DMCtrl(DMCtrl), .ALUOp(ALUOp));
  RegisterUnit registerunit_1 (
    .RD(IMOut[11:7]), .C(CLK), .RS1(IMOut[19:15]), .DataWr(DataWr), .RS2(IMOut[24:20]), .RuWr(RUWr),
    .RU_rs1(RU_rs1), .RU_rs2(RU_rs2), .a4(a4), .a5(a5), .a0(a0), .x0(x0), .s0(s0));
  // ImmGen immgen_1: pin names not known; wires that end beside it: IMOut[31:7], ImmSrc, ImmExt
  ResultSplitterDisplay resultsplitterdisplay_1 (
    .Result(a0), .R1(R1), .R2(R2), .R3(R3), .R4(R4), .R5(R5), .R6(R6), .R7(R7), .R8(R8));
  Multiplexer #(.Bits(32)) multiplexer_1 (.sel(ALUASrc), .in_0(RU_rs1), .in_1(OutPC), .out(multiplexer_1_out));
  Multiplexer #(.Bits(32)) multiplexer_2 (.sel(ALUBSrc), .in_0(RU_rs2), .in_1(ImmExt), .out(multiplexer_2_out));
  Seven_Seg_Hex seven_seg_hex_9 (.d(R8), .dp(1'b0));
  // BranchUnit branchunit_1: pin names not known; wires that end beside it: RU_rs1, RU_rs2, BrOp, branchunit_1_p4
  Seven_Seg_Hex seven_seg_hex_10 (.d(R7), .dp(1'b0));
  Seven_Seg_Hex seven_seg_hex_11 (.d(R6), .dp(1'b0));
  ALU_32bits alu_32bits_1 (
    .InA(multiplexer_1_out), .InB(multiplexer_2_out), .Sel(ALUOp), .Ca(out_1), .Cs(out_2), .Out(ALUOut));  // open: rdiv, rdivu
  Seven_Seg_Hex seven_seg_hex_12 (.d(R5), .dp(1'b0));
  Multiplexer #(.Bits(32)) multiplexer_3 (.sel(branchunit_1_p4), .in_0(SumPC), .in_1(ALUOut), .out(InPC));
  Seven_Seg_Hex seven_seg_hex_13 (.d(R4), .dp(1'b0));
  Seven_Seg_Hex seven_seg_hex_14 (.d(R3), .dp(1'b0));
  // DataMemory datamemory_1: pin names not known; wires that end beside it: ALUOut, RU_rs2, DMWr, DMCtrl, CLK, DMOut
  Seven_Seg_Hex seven_seg_hex_15 (.d(R2), .dp(1'b0));
  Seven_Seg_Hex seven_seg_hex_16 (.d(R1), .dp(1'b0));
  Multiplexer #(.Selector_Bits(2), .Bits(32)) multiplexer_4 (
    .sel(RUDataWrSrc), .in_0(ALUOut), .in_1(DMOut), .in_2(SumPC), .in_3({32{1'b0}}), .out(DataWr));

  // Other names for the same wires on the sheet: C1 = out_1; C2 = out_2; Opcode[6:0] = IMOut[6:0];
  //   RD[4:0] = IMOut[11:7]; Funct3[2:0] = IMOut[14:12]; RS1[4:0] = IMOut[19:15]; RS2[4:0] = IMOut[24:20];
  //   Funct7[6:0] = IMOut[31:25]

  // Notes on the sheet:
  //   CLK: Hz: 2147483647
  //   ImmExt: Inmediato generado extendido a 32 bits
  //   SALIDA DE LA ALU
  //   RESULTADO
endmodule
